# Fritzing sketch IoTMiniYonkuScetch (saved by Fritzing 0.9.4)
breadboards: 1

parts:
  L298N1 = L298N DC motor driver
  U1 = NodeMCU V1.0
  M1 = DC Motor
  VCC1 = Battery block 9V
  YwRobot_Power_Supply1 = YwRobot Breadboard Power Supply [part_number=545043]
  VCC2 = Battery block 9V
  JACK1 = 2.1mm Barrel Jack with Terminal Block
  LED2 = smd LED [color="Red (633nm)" package="0805 [SMD]"]
  LED3 = smd LED [color="Green (555nm)" package="0805 [SMD]"]
  LED1 = smd LED [color="Blue (430nm)" package="0805 [SMD]"]

nets:
  N1: L298N1.OUT1, M1.pin_1
  N2: L298N1.OUT2, M1.pin_2
  N3: L298N1.12V, VCC1.+
  GND: L298N1.GND, U1.GND, VCC1.-, YwRobot_Power_Supply1.GND, LED2.cathode, LED3.cathode, LED1.cathode
  N4: L298N1.ENA, U1.D7
  N5: L298N1.IN1, U1.D5
  N6: L298N1.IN2, U1.D6
  N7: U1.D1, LED2.anode
  N8: U1.D2, LED3.anode
  N9: U1.D8, LED1.anode
  VIN: U1.Vin, YwRobot_Power_Supply1.VCC
  N10: VCC2.-, JACK1.NEG
  N11: VCC2.+, JACK1.POS

custom parts:
  L298N DC motor driver: 2x DC motor driver with 78M05 positive voltage regulator (7..35 V) L298N: max 46 V, 2 A Set 5 V Enable jumper to enable 5 V regultor (needed for the L298N) and +5 V output at screw terminal or supply external +5 V at screw terminal Set ENA and/or ENB to +5 V to enable motor permanently or supply ENA and/or ENB with PWM signal IN1 and IN2 set rotation directory for motor A (OUT1/OUT2) IN2 and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
  NodeMCU V1.0: ESP8266 based NodeMCU
  YwRobot Breadboard Power Supply: The YwRobot Breadboard Power Supply (MB-V2) has two power rails; they can be 5V or 3V3. Power to the module can be provided through the female USB socket or through the A10 (female) 2.1mm power jack.

// code stored in the sketch: IoTMiniYonku.ino
#include <ESP8266WiFi.h>
#include <ESP8266WebServer.h>
#include <FS.h>

// Pin Define of NodeMCU made by AMICA
#define PIN_D1_BRAKE_LED 5
#define PIN_D2_CONNECT_STATE 4
#define PIN_D8_CONNECT_STATE 15
#define PIN_D5_IN1  14          // Motor Driver L298N IN1
#define PIN_D6_IN2  12          // Motor Driver L298N IN2
#define PIN_D7_EN_A 13          // Motor Driver L298N ENABLE PIN

// global variable
const char *ssid = "";          // Your WiFi SSID
const char *password = "";      // Your WiFi PASS
const char *pathRoot = "";      // HTML file Path
uint8_t buf[16384];             // Buffer for reading HTML
ESP8266WebServer server(80);    // Web server port

void handleRoot()
{                    
  if (server.method() == HTTP_POST)
  {
    String s = server.arg("ON");
    if (s == "Accel")
    {
      digitalWrite(PIN_D5_IN1, HIGH);
      digitalWrite(PIN_D6_IN2, LOW); 
      digitalWrite(PIN_D7_EN_A, HIGH); 
      digitalWrite(PIN_D1_BRAKE_LED, LOW);
    }
    else if (s == "Brake")
    {
      digitalWrite(PIN_D5_IN1, LOW);
      digitalWrite(PIN_D6_IN2, LOW);
      digitalWrite(PIN_D7_EN_A, LOW);
      digitalWrite(PIN_D1_BRAKE_LED, HIGH);
    } 
  }
  server.send(200, "text/html", (char *)buf); // Send the HTML file to the client
}

void serverConnectOk()
{
  Serial.println("serverConnectOk");
  for(int i = 0; i < 5; ++i)
  {
      digitalWrite(PIN_D8_CONNECT_STATE, HIGH);
      digitalWrite(PIN_D2_CONNECT_STATE, LOW);
      delay(200);
      digitalWrite(PIN_D8_CONNECT_STATE, LOW);
      digitalWrite(PIN_D2_CONNECT_STATE, HIGH);
      delay(200);
  }
  Serial.println("serverConnectOkEND");
      digitalWrite(PIN_D8_CONNECT_STATE, HIGH);
      digitalWrite(PIN_D2_CONNECT_STATE, HIGH);
}

void setup() 
{
  pinMode(PIN_D5_IN1, OUTPUT);
  pinMode(PIN_D6_IN2, OUTPUT);
  pinMode(PIN_D7_EN_A, OUTPUT);
  pinMode(PIN_D8_CONNECT_STATE, OUTPUT);
  pinMode(PIN_D2_CONNECT_STATE, OUTPUT);
  pinMode(PIN_D1_BRAKE_LED, OUTPUT);
  
  // Pin output init
  digitalWrite(PIN_D1_BRAKE_LED, HIGH);
  digitalWrite(PIN_D8_CONNECT_STATE, HIGH);
  digitalWrite(PIN_D2_CONNECT_STATE, LOW);
  digitalWrite(PIN_D5_IN1, LOW);
  digitalWrite(PIN_D6_IN2, LOW);
  digitalWrite(PIN_D7_EN_A, LOW);
  Serial.begin(115200);
  
  bool res = SPIFFS.begin();
  if (!res) 
  {
    Serial.println("SPIFFS.begin fail");
    return;
  }
  
  File htmlFile = SPIFFS.open(pathRoot, "r"); // Open the HTML file readonly

  if (!htmlFile)
  {
    Serial.println("open error");
  }
  
  size_t size = htmlFile.size();               // Size check the HTML file
  htmlFile.read(buf, size);                    // Read contents of HTML file into buffer
  htmlFile.close();                            // Close the HTML file
  
  WiFi.softAP(ssid, password);                 // Start the WiFi access point with the set SSID and password, IPAddress myIP = WiFi.softAPIP();
  IPAddress ip = WiFi.softAPIP();
  delay(500);
  Serial.println("");
  Serial.println(ssid + String(" starts..")); 
  Serial.print("this AP : "); 
  Serial.println(ip);
  
  server.on("/", handleRoot);                  // Specifies the function to be executed in response to a request from a client
  server.begin();                              // Boot the Web server.
  serverConnectOk();                           // Connect OK
}

void loop() 
{
  server.handleClient();                       // Process requests received from clients.
}
